// Logisim project CPU_single.circ as structural Verilog: 33 circuits, main circuit CPU
module CPU (
  input  Jen,
  input  [31:0] Jin,
  input  clk,
  input  rst,
  output InstDone,
  output [31:0] R0,
  output [31:0] R1,
  output [31:0] R2,
  output [31:0] R3,
  output [31:0] Jout,
  output [31:0] R4,
  output [31:0] R5,
  output [31:0] R6,
  output [31:0] R7,
  output [31:0] R8,
  output [31:0] R9,
  output [31:0] R10,
  output [31:0] R11,
  output [31:0] R12,
  output [31:0] R13,
  output [31:0] R14,
  output [31:0] R15,
  output [31:0] R16,
  output [31:0] R17,
  output [31:0] Total_Clock_Cycles,
  output [31:0] R18,
  output [31:0] R19,
  output [31:0] R20,
  output [31:0] R21,
  output [31:0] R22,
  output [31:0] Total_Issued_Instructions,
  output [31:0] R23,
  output [31:0] R24,
  output [31:0] R25,
  output [31:0] Total_Stalls,
  output [31:0] R26,
  output [31:0] R27,
  output [31:0] R28,
  output [31:0] R29,
  output [31:0] R30,
  output [31:0] R31
);

  wire alu_1_done, ALUSrc, and_1_out, control_1_alusrc, control_1_branch, control_1_memwrite,
       control_1_regwrite, exmem_1_instdone, exmem_1_memwrite, exmem_1_regwrite, HIWrite, idex_1_memwrite,
       idex_1_regwrite, LOWrite, memwb_1_instdone, not_1_out, not_2_out, not_3_out, not_4_out, PCSource,
       RegWrite, stall, Zero;
  wire [1:0] control_1_aluop, control_1_regdst, exmem_1_regdst, idex_1_aluop, idex_1_regdst, Jump, RegDst;
  wire [2:0] control_1_memtoreg, exmem_1_memtoreg, idex_1_memtoreg, MemtoReg;
  wire [3:0] aluop;
  wire [4:0] exmem_1_rd, exmem_1_rt, idex_1_rd, idex_1_rt, idex_1_shamt, multiplexer_3_out, rd, rs, rt,
       shamt, WB_rd, WB_rt;
  wire [5:0] funct, idex_1_funct, Opcode;
  wire [8:0] adder_1_out, adder_4_out, exmem_1_pc, idex_1_pc, ifid_1_pc, memwb_1_pc, multiplexer_1_out,
       multiplexer_2_out, PC_q;
  wire [31:0] adder_2_out, alu_1_res_high, alu_1_res_low, bit_extender_2_out, Data, DMEM_dout,
       exmem_1_aluresult, exmem_1_hi, exmem_1_lo, exmem_1_readdata2, HI_q, idex_1_imm, idex_1_readdata1,
       idex_1_readdata2, IMEM_dout, imm, Jout_t, LO_q, memwb_1_aluresult, memwb_1_hi, memwb_1_lo,
       memwb_1_memread, multiplexer_4_out, ReadData1, rf_1_regout2;

  not not_1 (not_1_out, stall);
  not not_2 (not_2_out, Jen);
  Register #(.width(9)) PC (.D(multiplexer_1_out), .en(and_1_out), .clk(clk), .Q(PC_q), .clr(rst));
  and and_1 (and_1_out, not_2_out, not_1_out);
  Multiplexer #(.select(2), .width(9)) multiplexer_1 (
    .in0(multiplexer_2_out), .in1({shamt[2:0], funct}), .in2(ReadData1[8:0]), .out(multiplexer_1_out),
    .sel(Jump));  // open: in3
  Adder #(.width(9)) adder_1 (.a(PC_q), .b(9'h1), .out(adder_1_out));  // open: cin, cout
  Multiplexer #(.width(9)) multiplexer_2 (
    .in0(adder_1_out), .in1(adder_4_out), .out(multiplexer_2_out), .sel(PCSource));
  MEM IMEM (.Wen(1'b0), .Jen(Jen), .clk(clk), .Addr(PC_q), .Jin(Jin), .Dout(IMEM_dout), .Jout(Jout_t));  // open: Din
  Register #(.width(32)) Cycles (.D(adder_2_out), .clk(clk), .Q(Total_Clock_Cycles), .clr(rst));  // open: en
  not not_3 (not_3_out, stall);
  Adder #(.width(32)) adder_2 (.a(Total_Clock_Cycles), .b(32'h1), .out(adder_2_out));  // open: cin, cout
  Adder #(.width(32)) adder_3 (
    .a(Total_Clock_Cycles), .b(32'hfffffffc), .out(Total_Issued_Instructions));  // open: cin, cout
  IFID ifid_1 (
    .WriteEnable(not_3_out), .PC_in(adder_1_out), .Instruction_in(IMEM_dout), .clk(clk), .reset(rst),
    .PC(ifid_1_pc), .Instruction({Opcode, rs, rt, rd, shamt, funct}));
  assign imm = {{16{rd[4]}}, {rd, shamt, funct}};  // Bit_Extender bit_extender_1
  Multiplexer #(.select(2), .width(5)) multiplexer_3 (
    .in0(WB_rd), .in1(WB_rt), .in2({5{1'b1}}), .out(multiplexer_3_out), .sel(RegDst));  // open: in3
  Adder #(.width(9)) adder_4 (.a(ifid_1_pc), .b({shamt[2:0], funct}), .out(adder_4_out));  // open: cin, cout
  RF rf_1 (
    .Read0(rs), .Read1(rt), .WriteReg(RegWrite), .Write(multiplexer_3_out), .clk(clk), .rst(rst),
    .Data(Data), .R0(R0), .R1(R1), .R2(R2), .R3(R3), .R4(R4), .R5(R5), .R6(R6), .R7(R7), .R8(R8), .R9(R9),
    .R10(R10), .R11(R11), .R12(R12), .R13(R13), .R14(R14), .R15(R15), .R16(R16), .R17(R17), .R18(R18),
    .R19(R19), .R20(R20), .R21(R21), .R22(R22), .R23(R23), .R24(R24), .R25(R25), .R26(R26), .R27(R27),
    .R28(R28), .R29(R29), .R30(R30), .R31(R31), .RegOut2(rf_1_regout2), .RegOut1(ReadData1));
  and and_2 (PCSource, ~Zero, control_1_branch);  // AND_Gate
  Control control_1 (
    .opcode(Opcode), .funct(funct), .Branch(control_1_branch), .Jump(Jump), .RegDst(control_1_regdst),
    .RegWrite(control_1_regwrite), .ALUOp(control_1_aluop), .ALUSrc(control_1_alusrc),
    .MemWrite(control_1_memwrite), .MemtoReg(control_1_memtoreg));
  not not_4 (not_4_out, stall);
  Comparator #(.width(32)) comparator_1 (.a(ReadData1), .b(rf_1_regout2), .eq(Zero));  // open: gt, lt
  IDEX idex_1 (
    .clk(clk), .PC_in(ifid_1_pc), .funct_in(funct), .shamt_in(shamt), .imm_in(imm), .ReadData1_in(ReadData1),
    .ReadData2_in(rf_1_regout2), .rt_in(rt), .rd_in(rd), .RegDst_in(control_1_regdst),
    .RegWrite_in(control_1_regwrite), .ALUOp_in(control_1_aluop), .ALUSrc_in(control_1_alusrc),
    .MemWrite_in(control_1_memwrite), .MemtoReg_in(control_1_memtoreg), .WriteEnable(not_4_out), .reset(rst),
    .PC(idex_1_pc), .funct(idex_1_funct), .shamt(idex_1_shamt), .imm(idex_1_imm),
    .ReadData1(idex_1_readdata1), .ReadData2(idex_1_readdata2), .rt(idex_1_rt), .rd(idex_1_rd),
    .RegDst(idex_1_regdst), .MemtoReg(idex_1_memtoreg), .RegWrite(idex_1_regwrite), .ALUOp(idex_1_aluop),
    .ALUSrc(ALUSrc), .MemWrite(idex_1_memwrite));
  Multiplexer #(.width(32)) multiplexer_4 (
    .in0(idex_1_imm), .in1(idex_1_readdata2), .out(multiplexer_4_out), .sel(ALUSrc));
  ALUControl alucontrol_1 (
    .funct(idex_1_funct), .ALUOp(idex_1_aluop), .operation(aluop), .HIWrite(HIWrite), .LOWrite(LOWrite));
  ALU alu_1 (
    .clk(clk), .a(idex_1_readdata1), .b(multiplexer_4_out), .aluop(aluop), .shamt(idex_1_shamt), .rst(rst),
    .done(alu_1_done), .res_high(alu_1_res_high), .res_low(alu_1_res_low));  // open: output_inverted, output_inc, Zero
  not not_5 (stall, alu_1_done);
  Register #(.width(32)) HI (.D(alu_1_res_high), .en(HIWrite), .clk(clk), .Q(HI_q), .clr(rst));
  Register #(.width(32)) LO (.D(alu_1_res_low), .en(LOWrite), .clk(clk), .Q(LO_q), .clr(rst));
  EXMEM exmem_1 (
    .clk(clk), .ReadData2_in(idex_1_readdata2), .RegDst_in(idex_1_regdst), .rt_in(idex_1_rt),
    .rd_in(idex_1_rd), .InstDone_in(alu_1_done), .RegWrite_in(idex_1_regwrite),
    .MemWrite_in(idex_1_memwrite), .MemtoReg_in(idex_1_memtoreg), .PC_in(idex_1_pc),
    .ALUResult_in(alu_1_res_low), .HI_in(HI_q), .LO_in(LO_q), .WriteEnable(1'b1), .reset(rst),
    .rt(exmem_1_rt), .rd(exmem_1_rd), .PC(exmem_1_pc), .ReadData2(exmem_1_readdata2),
    .RegDst(exmem_1_regdst), .MemtoReg(exmem_1_memtoreg), .ALUResult(exmem_1_aluresult), .HI(exmem_1_hi),
    .LO(exmem_1_lo), .InstDone(exmem_1_instdone), .RegWrite(exmem_1_regwrite), .MemWrite(exmem_1_memwrite));
  MEM DMEM (
    .Wen(exmem_1_memwrite), .Jen(Jen), .clk(clk), .Addr(exmem_1_aluresult[8:0]), .Din(exmem_1_readdata2),
    .Jin(Jout_t), .Dout(DMEM_dout), .Jout(Jout));
  MEMWB memwb_1 (
    .clk(clk), .rt_in(exmem_1_rt), .rd_in(exmem_1_rd), .InstDone_in(exmem_1_instdone),
    .RegDst_in(exmem_1_regdst), .RegWrite_in(exmem_1_regwrite), .MemtoReg_in(exmem_1_memtoreg),
    .PC_in(exmem_1_pc), .HI_in(exmem_1_hi), .LO_in(exmem_1_lo), .MemRead_in(DMEM_dout),
    .ALUResult_in(exmem_1_aluresult), .WriteEnable(1'b1), .reset(rst), .rt(WB_rt), .rd(WB_rd),
    .PC(memwb_1_pc), .RegDst(RegDst), .MemtoReg(MemtoReg), .HI(memwb_1_hi), .LO(memwb_1_lo),
    .MemRead(memwb_1_memread), .ALUResult(memwb_1_aluresult), .InstDone(memwb_1_instdone), .RegWrite(RegWrite));
  D_Flip_Flop d_ff_1 (.D(memwb_1_instdone), .clk(clk), .Q(InstDone), .reset(rst));  // open: Qn, preset
  assign bit_extender_2_out = {{23{memwb_1_pc[8]}}, memwb_1_pc};  // Bit_Extender bit_extender_2
  Multiplexer #(.select(3), .width(32)) multiplexer_5 (
    .in0(memwb_1_aluresult), .in1(memwb_1_memread), .in2(bit_extender_2_out), .in3(memwb_1_hi),
    .in4(memwb_1_lo), .out(Data), .sel(MemtoReg));  // open: in5, in6, in7

  assign Total_Stalls = {32{1'b0}};

  // Other names for the same wires on the sheet: reset = rst
endmodule

module ALU (
  input  [3:0] aluop,
  input  [31:0] a,
  input  [31:0] b,
  input  rst,
  input  clk,
  input  [4:0] shamt,
  input  output_inverted,
  input  output_inc,
  output [31:0] res_low,
  output done,
  output [31:0] res_high,
  output Zero
);

  wire adder_1_cout, comparator_1_eq, comparator_2_eq, comparator_4_eq, comparator_5_eq, d_ff_1_q,
       div_1_done, mult_1_done, not_1_out, not_2_out, or_1_out, or_2_out;
  wire [0:0] comparator_3_lt;
  wire [31:0] add_1_res_high, add_1_res_low, andd_1_res_high, andd_1_res_low, bit_extender_1_out,
       clo_1_res_high, clo_1_res_low, clz_1_res_high, clz_1_res_low, div_1_quotient, div_1_remainder,
       mult_1_res_hi, mult_1_res_lo, multiplexer_1_out, multiplexer_3_out, multiplexer_4_out,
       multiplexer_5_out, not_3_out, not_4_out, orr_1_res_high, orr_1_res_low, register_1_q, register_2_q,
       rotr_1_res_high, rotr_1_res_low, shll_1_res_high, shll_1_res_low, shll_2_res_high, shll_2_res_low,
       shra_1_res_high, shra_1_res_low, shrl_1_res_high, shrl_1_res_low, sub_1_res_high, sub_1_res_low,
       xorr_1_res_high, xorr_1_res_low;

  Register #(.width(32)) register_1 (.D(a), .clk(clk), .Q(register_1_q), .clr(rst));  // open: en
  Register #(.width(32)) register_2 (.D(b), .clk(clk), .Q(register_2_q), .clr(rst));  // open: en
  Comparator #(.width(32)) comparator_1 (.a(a), .b(register_1_q), .eq(comparator_1_eq));  // open: gt, lt
  not not_1 (not_1_out, comparator_1_eq);
  not not_2 (not_2_out, comparator_2_eq);
  Comparator #(.width(32)) comparator_2 (.a(b), .b(register_2_q), .eq(comparator_2_eq));  // open: gt, lt
  or or_1 (or_1_out, not_1_out, not_2_out);
  D_Flip_Flop d_ff_1 (.D(or_1_out), .clk(clk), .Q(d_ff_1_q), .reset(rst));  // open: Qn, preset
  or or_2 (or_2_out, or_1_out, d_ff_1_q);
  assign bit_extender_1_out = {{27{1'b0}}, shamt};  // Bit_Extender bit_extender_1
  Comparator #(.width(32)) comparator_3 (.a(a), .b(b), .lt(comparator_3_lt[0]));  // open: gt, eq
  Add add_1 (.A(a), .B(b), .res_low(add_1_res_low), .res_high(add_1_res_high));
  Sub sub_1 (.a(a), .b(b), .res_low(sub_1_res_low), .res_high(sub_1_res_high));
  MULT mult_1 (
    .a(a), .b(b), .start(or_2_out), .rst_n(rst), .clk(clk), .done(mult_1_done), .res_lo(mult_1_res_lo),
    .res_hi(mult_1_res_hi));
  Div div_1 (
    .dividend(a), .divisor(b), .start(or_2_out), .clk(clk), .remainder(div_1_remainder),
    .quotient(div_1_quotient), .done(div_1_done));
  ANDD andd_1 (.a(a), .b(b), .res_low(andd_1_res_low), .res_high(andd_1_res_high));
  ORR orr_1 (.A(a), .B(b), .res_low(orr_1_res_low), .res_high(orr_1_res_high));
  XORR xorr_1 (.a(a), .b(b), .res_low(xorr_1_res_low), .res_high(xorr_1_res_high));
  Clo clo_1 (.a(a), .res_low(clo_1_res_low), .res_high(clo_1_res_high));
  Clz clz_1 (.A(a), .res_low(clz_1_res_low), .res_high(clz_1_res_high));
  SHLL shll_1 (.a(a), .b(b), .res_low(shll_1_res_low), .res_high(shll_1_res_high));
  SHRL shrl_1 (.a(a), .b(b), .res_low(shrl_1_res_low), .res_high(shrl_1_res_high));
  SHRA shra_1 (.a(a), .b(b), .res_low(shra_1_res_low), .res_high(shra_1_res_high));
  Rotr rotr_1 (.A(a), .B(b), .res_low(rotr_1_res_low), .res_high(rotr_1_res_high));
  SHLL shll_2 (.a(b), .b(bit_extender_1_out), .res_low(shll_2_res_low), .res_high(shll_2_res_high));
  Multiplexer #(.select(4), .width(32)) multiplexer_1 (
    .in0(add_1_res_low), .in1(sub_1_res_low), .in2(mult_1_res_lo), .in3(div_1_quotient),
    .in4(andd_1_res_low), .in5(orr_1_res_low), .in6(xorr_1_res_low), .in7(clo_1_res_low),
    .in8(clz_1_res_low), .in9(shll_1_res_low), .in10(shrl_1_res_low), .in11(shra_1_res_low),
    .in12(rotr_1_res_low), .in13({{31{1'b0}}, comparator_3_lt[0]}), .in14(shll_2_res_low),
    .out(multiplexer_1_out), .sel(aluop));  // open: in15
  Multiplexer #(.select(4)) multiplexer_2 (
    .in0(1'b1), .in1(1'b1), .in2(mult_1_done), .in3(div_1_done), .in4(1'b1), .in5(1'b1), .in6(1'b1),
    .in7(1'b1), .in8(1'b1), .in9(1'b1), .in10(1'b1), .in11(1'b1), .in12(1'b1), .in13(1'b1), .in14(1'b1),
    .out(done), .sel(aluop));  // open: in15
  Multiplexer #(.select(4), .width(32)) multiplexer_3 (
    .in0(add_1_res_high), .in1(sub_1_res_high), .in2(mult_1_res_hi), .in3(div_1_remainder),
    .in4(andd_1_res_high), .in5(orr_1_res_high), .in6(xorr_1_res_high), .in7(clo_1_res_high),
    .in8(clz_1_res_high), .in9(shll_1_res_high), .in10(shrl_1_res_high), .in11(shra_1_res_high),
    .in12(rotr_1_res_high), .in13({32{1'b0}}), .in14(shll_2_res_high), .out(multiplexer_3_out), .sel(aluop));  // open: in15
  assign not_3_out = ~multiplexer_1_out;  // NOT_Gate not_3, 32 bits wide
  Multiplexer #(.width(32)) multiplexer_4 (
    .in0(multiplexer_3_out), .in1(not_4_out), .out(multiplexer_4_out), .sel(output_inverted));
  assign not_4_out = ~multiplexer_3_out;  // NOT_Gate not_4, 32 bits wide
  Multiplexer #(.width(32)) multiplexer_5 (
    .in0(multiplexer_1_out), .in1(not_3_out), .out(multiplexer_5_out), .sel(output_inverted));
  Adder #(.width(32)) adder_1 (
    .a(multiplexer_5_out), .b({32{1'b0}}), .out(res_low), .cin(output_inc), .cout(adder_1_cout));
  Adder #(.width(32)) adder_2 (
    .a(multiplexer_4_out), .b({32{1'b0}}), .out(res_high), .cin(adder_1_cout));  // open: cout
  Comparator #(.width(32)) comparator_4 (.a(res_low), .b({32{1'b0}}), .eq(comparator_4_eq));  // open: gt, lt
  Comparator #(.width(32)) comparator_5 (.a({32{1'b0}}), .b(res_high), .eq(comparator_5_eq));  // open: gt, lt
  and and_1 (Zero, comparator_4_eq, comparator_5_eq);
endmodule

module Div (
  input  [31:0] dividend,
  input  [31:0] divisor,
  input  start,
  input  clk,
  output [31:0] remainder,
  output [31:0] quotient,
  output done
);

  wire and_1_out, and_2_out, and_3_out, and_4_out, and_5_out, comparator_1_eq, comparator_1_gt,
       comparator_2_lt, DIVID_q, DIVID_qn, doneFF_q, INIT_q, INIT_qn, multiplexer_5_out, not_1_out, or_1_out,
       or_2_out, or_3_out, or_4_out, or_5_out;
  wire [0:0] not_2_out, R_divid_q_2;
  wire [1:0] and_7_out;
  wire [7:0] counter_q, multiplexer_4_out, subtractor_1_out;
  wire [31:0] multiplexer_1_out, multiplexer_2_out, multiplexer_3_out, R_divis_q, subtractor_2_out;
  wire [31:1] R_divid_q;

  and and_1 (and_1_out, not_1_out, DIVID_qn);
  and and_2 (and_2_out, INIT_qn, and_1_out);
  and and_3 (and_3_out, comparator_1_eq, DIVID_q);
  not not_1 (not_1_out, start);
  D_Flip_Flop INIT (.D(or_1_out), .clk(clk), .Q(INIT_q), .Qn(INIT_qn), .preset(start));  // open: reset
  or or_1 (or_1_out, and_1_out, and_3_out);
  and and_4 (and_4_out, start, INIT_q);
  and and_5 (and_5_out, comparator_1_gt, DIVID_q);
  and and_6 (and_7_out[1], INIT_q, start);
  D_Flip_Flop DIVID (.D(or_2_out), .clk(clk), .Q(DIVID_q), .Qn(DIVID_qn));  // open: preset, reset
  or or_2 (or_2_out, and_4_out, and_5_out);
  and and_7 (and_7_out[0], not_2_out[0], DIVID_q);
  or or_3 (or_3_out, and_7_out[1], DIVID_q);
  Multiplexer #(.select(2), .width(32)) multiplexer_1 (
    .in0({remainder[30:0], R_divid_q_2[0]}), .in1(subtractor_2_out), .in2({32{1'b0}}), .in3({32{1'b0}}),
    .out(multiplexer_1_out), .sel(and_7_out));
  Multiplexer #(.width(32)) multiplexer_2 (
    .in0({R_divid_q, 1'b0}), .in1(dividend), .out(multiplexer_2_out), .sel(and_7_out[1]));
  Multiplexer #(.width(32)) multiplexer_3 (
    .in0({32{1'b0}}), .in1({quotient[30:0], not_2_out[0]}), .out(multiplexer_3_out), .sel(DIVID_q));
  Multiplexer #(.width(8)) multiplexer_4 (
    .in0(subtractor_1_out), .in1(8'h20), .out(multiplexer_4_out), .sel(and_7_out[1]));
  Register #(.width(32)) R_rem (.D(multiplexer_1_out), .en(or_3_out), .clk(clk), .Q(remainder), .clr(and_2_out));
  Register #(.width(32)) R_divid (
    .D(multiplexer_2_out), .en(or_3_out), .clk(clk), .Q({R_divid_q_2[0], R_divid_q}), .clr(and_2_out));
  Register #(.width(32)) R_divis (.D(divisor), .en(and_7_out[1]), .clk(clk), .Q(R_divis_q), .clr(and_2_out));
  Register #(.width(32)) R_q (.D(multiplexer_3_out), .en(or_3_out), .clk(clk), .Q(quotient), .clr(and_2_out));
  Register counter (.D(multiplexer_4_out), .en(or_3_out), .clk(clk), .Q(counter_q), .clr(and_2_out));
  D_Flip_Flop d_ff_1 (.D(or_5_out), .clk(clk), .Q(done), .reset(and_2_out));  // open: Qn, preset
  Comparator comparator_1 (.a(counter_q), .b(8'h1), .gt(comparator_1_gt), .eq(comparator_1_eq));  // open: lt
  Subtractor subtractor_1 (.a(counter_q), .b(8'h1), .out(subtractor_1_out));  // open: bin, bout
  Comparator #(.mode("unsigned"), .width(32)) comparator_2 (
    .a({remainder[30:0], R_divid_q_2[0]}), .b(R_divis_q), .lt(comparator_2_lt));  // open: gt, eq
  Subtractor #(.width(32)) subtractor_2 (
    .a({remainder[30:0], R_divid_q_2[0]}), .b(R_divis_q), .out(subtractor_2_out));  // open: bin, bout
  not not_2 (not_2_out[0], comparator_2_lt);
  Register #(.width(1)) doneFF (.D(multiplexer_5_out), .en(or_4_out), .clk(clk), .Q(doneFF_q), .clr(and_2_out));
  Multiplexer multiplexer_5 (.in0(and_3_out), .in1(1'b0), .out(multiplexer_5_out), .sel(and_7_out[1]));
  or or_4 (or_4_out, and_7_out[1], and_3_out);
  or or_5 (or_5_out, doneFF_q, and_3_out);
endmodule

module ANDD (
  input  [31:0] a,
  input  [31:0] b,
  output [31:0] res_low,
  output [31:0] res_high
);

  assign res_low = a & b;  // AND_Gate and_1, 32 bits wide

  assign res_high = {32{1'b0}};
endmodule

module XORR (
  input  [31:0] a,
  input  [31:0] b,
  output [31:0] res_low,
  output [31:0] res_high
);

  assign res_low = a ^ b;  // XOR_Gate xor_1, 32 bits wide

  assign res_high = {32{1'b0}};
endmodule

module Sub (
  input  [31:0] a,
  input  [31:0] b,
  output [31:0] res_low,
  output [31:0] res_high
);

  wire comparator_1_lt;

  Comparator #(.mode("unsigned"), .width(32)) comparator_1 (.a(a), .b(b), .lt(comparator_1_lt));  // open: gt, eq
  Subtractor #(.width(32)) subtractor_1 (.a(a), .b(b), .out(res_low));  // open: bin, bout
  assign res_high = {{31{comparator_1_lt}}, comparator_1_lt};  // Bit_Extender bit_extender_1
endmodule

module SHLL (
  input  [31:0] a,
  input  [31:0] b,
  output [31:0] res_low,
  output [31:0] res_high
);

  wire [31:0] not_1_out;
  wire [63:0] multiplexer_1_out, multiplexer_2_out, multiplexer_4_out;
  wire [63:8] multiplexer_3_out;
  wire [63:56] multiplexer_3_out_2;

  assign not_1_out = ~b;  // NOT_Gate not_1, 32 bits wide
  Multiplexer #(.width(64)) multiplexer_1 (
    .in0({{31{1'b0}}, a, 1'b0}), .in1({{32{1'b0}}, a}), .out(multiplexer_1_out), .sel(not_1_out[0]));
  Multiplexer #(.width(64)) multiplexer_2 (
    .in0({multiplexer_1_out[61:0], 2'b00}), .in1(multiplexer_1_out), .out(multiplexer_2_out),
    .sel(not_1_out[1]));
  Multiplexer #(.width(64)) multiplexer_3 (
    .in0({multiplexer_2_out[59:0], 4'b0000}), .in1(multiplexer_2_out),
    .out({multiplexer_3_out_2, multiplexer_3_out}), .sel(not_1_out[2]));
  Multiplexer #(.width(64)) multiplexer_4 (
    .in0({multiplexer_3_out, {8{1'b0}}}), .in1({multiplexer_3_out_2, multiplexer_3_out}),
    .out(multiplexer_4_out), .sel(not_1_out[3]));
  Multiplexer #(.width(64)) multiplexer_5 (
    .in0({multiplexer_4_out[47:0], {16{1'b0}}}), .in1(multiplexer_4_out), .out({res_high, res_low}),
    .sel(not_1_out[4]));
endmodule

module SHRL (
  input  [31:0] a,
  input  [31:0] b,
  output [31:0] res_low,
  output [31:0] res_high
);

  wire [7:0] multiplexer_3_out;
  wire [23:0] multiplexer_3_out_2;
  wire [31:0] multiplexer_1_out, multiplexer_2_out, multiplexer_4_out;

  Multiplexer #(.width(32)) multiplexer_1 (.in0(a), .in1({1'b0, a[31:1]}), .out(multiplexer_1_out), .sel(b[0]));
  Multiplexer #(.width(32)) multiplexer_2 (
    .in0(multiplexer_1_out), .in1({2'b00, multiplexer_1_out[31:2]}), .out(multiplexer_2_out), .sel(b[1]));
  Multiplexer #(.width(32)) multiplexer_3 (
    .in0(multiplexer_2_out), .in1({4'b0000, multiplexer_2_out[31:4]}),
    .out({multiplexer_3_out_2, multiplexer_3_out}), .sel(b[2]));
  Multiplexer #(.width(32)) multiplexer_4 (
    .in0({multiplexer_3_out_2, multiplexer_3_out}), .in1({{8{1'b0}}, multiplexer_3_out_2}),
    .out(multiplexer_4_out), .sel(b[3]));
  Multiplexer #(.width(32)) multiplexer_5 (
    .in0(multiplexer_4_out), .in1({{16{1'b0}}, multiplexer_4_out[31:16]}), .out(res_low), .sel(b[4]));

  assign res_high = {32{1'b0}};
endmodule

module SHRA (
  input  [31:0] a,
  input  [31:0] b,
  output [31:0] res_low,
  output [31:0] res_high
);

  wire [1:0] bit_extender_1_out;
  wire [3:0] bit_extender_2_out;
  wire [7:0] bit_extender_3_out, multiplexer_3_out;
  wire [15:0] bit_extender_4_out;
  wire [23:0] multiplexer_3_out_2;
  wire [31:0] multiplexer_1_out, multiplexer_2_out, multiplexer_4_out;

  Multiplexer #(.width(32)) multiplexer_1 (.in0(a), .in1({{2{a[31]}}, a[30:1]}), .out(multiplexer_1_out), .sel(b[0]));
  assign bit_extender_1_out = {{1{a[31]}}, a[31]};  // Bit_Extender bit_extender_1
  Multiplexer #(.width(32)) multiplexer_2 (
    .in0(multiplexer_1_out), .in1({bit_extender_1_out, multiplexer_1_out[31:2]}), .out(multiplexer_2_out),
    .sel(b[1]));
  assign bit_extender_2_out = {{3{a[31]}}, a[31]};  // Bit_Extender bit_extender_2
  Multiplexer #(.width(32)) multiplexer_3 (
    .in0(multiplexer_2_out), .in1({bit_extender_2_out, multiplexer_2_out[31:4]}),
    .out({multiplexer_3_out_2, multiplexer_3_out}), .sel(b[2]));
  assign bit_extender_3_out = {{7{a[31]}}, a[31]};  // Bit_Extender bit_extender_3
  Multiplexer #(.width(32)) multiplexer_4 (
    .in0({multiplexer_3_out_2, multiplexer_3_out}), .in1({bit_extender_3_out, multiplexer_3_out_2}),
    .out(multiplexer_4_out), .sel(b[3]));
  assign bit_extender_4_out = {{15{a[31]}}, a[31]};  // Bit_Extender bit_extender_4
  Multiplexer #(.width(32)) multiplexer_5 (
    .in0(multiplexer_4_out), .in1({bit_extender_4_out, multiplexer_4_out[31:16]}), .out(res_low), .sel(b[4]));
  assign res_high = {{31{a[31]}}, a[31]};  // Bit_Extender bit_extender_5
endmodule

module ORR (
  input  [31:0] A,
  input  [31:0] B,
  output [31:0] res_low,
  output [31:0] res_high
);

  assign res_low = A | B;  // OR_Gate or_1, 32 bits wide

  assign res_high = {32{1'b0}};
endmodule

module Add (
  input  [31:0] A,
  input  [31:0] B,
  output [31:0] res_low,
  output [31:0] res_high
);

  wire adder_1_cout;

  Adder #(.width(32)) adder_1 (.a(A), .b(B), .out(res_low), .cout(adder_1_cout));  // open: cin
  Adder #(.width(32)) adder_2 (.a({32{1'b0}}), .b({32{1'b0}}), .out(res_high), .cin(adder_1_cout));  // open: cout
endmodule

module ROTR1 (
  input  [31:0] A,
  output [31:0] result
);


  assign result = {A[0], A[31:1]};
endmodule

module ROTR2 (
  input  [31:0] A,
  output [31:0] result
);

  wire [31:0] ROT1_result;

  ROTR1 ROT1 (.A(A), .result(ROT1_result));
  ROTR1 ROT2 (.A(ROT1_result), .result(result));
endmodule

module ROTR4 (
  input  [31:0] A,
  output [31:0] result
);

  wire [31:0] ROT1_result;

  ROTR2 ROT1 (.A(A), .result(ROT1_result));
  ROTR2 ROT2 (.A(ROT1_result), .result(result));
endmodule

module ROTR8 (
  input  [31:0] A,
  output [31:0] result
);

  wire [31:0] ROT1_result;

  ROTR4 ROT1 (.A(A), .result(ROT1_result));
  ROTR4 ROT2 (.A(ROT1_result), .result(result));
endmodule

module ROTR16 (
  input  [31:0] A,
  output [31:0] result
);

  wire [31:0] ROT1_result;

  ROTR8 ROT1 (.A(A), .result(ROT1_result));
  ROTR8 ROT2 (.A(ROT1_result), .result(result));
endmodule

module Rotr (
  input  [31:0] A,
  input  [31:0] B,
  output [31:0] res_low,
  output [31:0] res_high
);

  wire [31:0] multiplexer_1_out, multiplexer_2_out, multiplexer_3_out, multiplexer_4_out, ROT1_result,
       ROT2_result, ROT4_result, ROT8_result, ROT16_result;

  Multiplexer #(.width(32)) multiplexer_1 (.in0(A), .in1(ROT1_result), .out(multiplexer_1_out), .sel(B[0]));
  ROTR1 ROT1 (.A(A), .result(ROT1_result));
  Multiplexer #(.width(32)) multiplexer_2 (
    .in0(multiplexer_1_out), .in1(ROT2_result), .out(multiplexer_2_out), .sel(B[1]));
  ROTR2 ROT2 (.A(multiplexer_1_out), .result(ROT2_result));
  Multiplexer #(.width(32)) multiplexer_3 (
    .in0(multiplexer_2_out), .in1(ROT4_result), .out(multiplexer_3_out), .sel(B[2]));
  ROTR4 ROT4 (.A(multiplexer_2_out), .result(ROT4_result));
  ROTR8 ROT8 (.A(multiplexer_3_out), .result(ROT8_result));
  Multiplexer #(.width(32)) multiplexer_4 (
    .in0(multiplexer_3_out), .in1(ROT8_result), .out(multiplexer_4_out), .sel(B[3]));
  Multiplexer #(.width(32)) multiplexer_5 (.in0(multiplexer_4_out), .in1(ROT16_result), .out(res_low), .sel(B[4]));
  ROTR16 ROT16 (.A(multiplexer_4_out), .result(ROT16_result));

  assign res_high = {32{1'b0}};
endmodule

module MULT (
  input  [31:0] a,
  input  [31:0] b,
  input  start,
  input  rst_n,
  input  clk,
  output done,
  output [31:0] res_lo,
  output [31:0] res_hi
);

  wire not_1_out, or_1_out;
  wire [7:0] adder_1_out, counter_q;
  wire [63:0] bit_extender_1_out, bit_extender_2_out, Carry_q, level1_carry, level1_sum, level2_carry,
       level2_sum, multiplexer_1_out, multiplexer_2_out, multiplexer_3_out, multiplexer_4_out,
       Multiplicand_q, Multiplier_q, SHL1_b, SHL2_b, SHR1_b, SHR2_b, Sum_q;

  Adder adder_1 (.a(8'h1), .b(counter_q), .out(adder_1_out));  // open: cin, cout
  or or_1 (or_1_out, start, rst_n);
  Register counter (.D(adder_1_out), .en(not_1_out), .clk(clk), .Q(counter_q), .clr(or_1_out));
  Comparator comparator_1 (.a(counter_q), .b(8'h10), .eq(done));  // open: gt, lt
  not not_1 (not_1_out, done);
  SHL64 SHL2 (.A(SHL1_b), .B(SHL2_b));
  SHR64 SHR2 (.A(SHR1_b), .B(SHR2_b));
  assign bit_extender_1_out = {{32{1'b0}}, a};  // Bit_Extender bit_extender_1
  SHL64 SHL1 (.A(Multiplicand_q), .B(SHL1_b));
  SHR64 SHR1 (.A(Multiplier_q), .B(SHR1_b));
  assign bit_extender_2_out = {{32{1'b0}}, b};  // Bit_Extender bit_extender_2
  Multiplexer #(.width(64)) multiplexer_1 (
    .in0(SHL2_b), .in1(bit_extender_1_out), .out(multiplexer_1_out), .sel(start));
  Multiplexer #(.width(64)) multiplexer_2 (
    .in0(SHR2_b), .in1(bit_extender_2_out), .out(multiplexer_2_out), .sel(start));
  Register #(.width(64)) Multiplicand (.D(multiplexer_1_out), .en(1'b1), .clk(clk), .Q(Multiplicand_q), .clr(rst_n));
  Register #(.width(64)) Multiplier (.D(multiplexer_2_out), .en(1'b1), .clk(clk), .Q(Multiplier_q), .clr(rst_n));
  Register #(.width(64)) Sum (.D(level2_sum), .en(1'b1), .clk(clk), .Q(Sum_q), .clr(or_1_out));
  Register #(.width(64)) Carry (.D(level2_carry), .en(1'b1), .clk(clk), .Q(Carry_q), .clr(or_1_out));
  Multiplexer #(.width(64)) multiplexer_3 (
    .in0({64{1'b0}}), .in1(SHL1_b), .out(multiplexer_3_out), .sel(Multiplier_q[1]));
  Multiplexer #(.width(64)) multiplexer_4 (
    .in0({64{1'b0}}), .in1(Multiplicand_q), .out(multiplexer_4_out), .sel(Multiplier_q[0]));
  Adder #(.width(64)) adder_2 (.a(Sum_q), .b(Carry_q), .out({res_hi, res_lo}));  // open: cin, cout
  CSA level1 (.X(multiplexer_3_out), .Y(multiplexer_4_out), .Z(Sum_q), .sum(level1_sum), .carry(level1_carry));
  CSA level2 (.X(level1_sum), .Y(level1_carry), .Z(Carry_q), .sum(level2_sum), .carry(level2_carry));
endmodule

module CSA (
  input  [63:0] X,
  input  [63:0] Y,
  input  [63:0] Z,
  output [63:0] sum,
  output [63:0] carry
);

  wire [63:0] and_1_out, and_2_out, and_3_out, or_1_out;

  assign and_1_out = X & Y;  // AND_Gate and_1, 64 bits wide
  assign and_2_out = X & Z;  // AND_Gate and_2, 64 bits wide
  assign and_3_out = Y & Z;  // AND_Gate and_3, 64 bits wide
  assign sum = X ^ Y ^ Z;  // XOR_Gate xor_1, 64 bits wide
  assign or_1_out = and_1_out | and_2_out | and_3_out;  // OR_Gate or_1, 64 bits wide
  SHL64 shift (.A(or_1_out), .B(carry));
endmodule

module SHL64 (
  input  [63:0] A,
  output [63:0] B
);

  not not_1 (B[0], 1'b1);

  assign B[63:1] = A[62:0];
endmodule

module SHR64 (
  input  [63:0] A,
  output [63:0] B
);

  not not_1 (B[63], 1'b1);

  assign B[62:0] = A[63:1];
endmodule

module Clz (
  input  [31:0] A,
  output [31:0] res_low,
  output [31:0] res_high
);

  wire and_5_out, comparator_1_eq, comparator_2_eq, comparator_3_eq, comparator_4_eq, not_1_out;
  wire [0:0] not_2_out;
  wire [1:0] multiplexer_4_out;
  wire [3:0] multiplexer_3_out;
  wire [7:0] multiplexer_2_out;
  wire [15:0] multiplexer_1_out;
  wire [31:0] adder_1_out, adder_2_out, adder_3_out, and_1_out, and_2_out, and_3_out, and_4_out,
       bit_extender_1_out, bit_extender_2_out, bit_extender_3_out, bit_extender_4_out;

  Comparator #(.width(16)) comparator_1 (.a(A[31:16]), .b({16{1'b0}}), .eq(comparator_1_eq));  // open: gt, lt
  Multiplexer #(.width(16)) multiplexer_1 (
    .in0(A[31:16]), .in1(A[15:0]), .out(multiplexer_1_out), .sel(comparator_1_eq));
  assign bit_extender_1_out = {{31{comparator_1_eq}}, comparator_1_eq};  // Bit_Extender bit_extender_1
  Comparator comparator_2 (.a(multiplexer_1_out[15:8]), .b({8{1'b0}}), .eq(comparator_2_eq));  // open: gt, lt
  assign and_1_out = bit_extender_1_out & 32'h10;  // AND_Gate and_1, 32 bits wide
  Multiplexer #(.width(8)) multiplexer_2 (
    .in0(multiplexer_1_out[15:8]), .in1(multiplexer_1_out[7:0]), .out(multiplexer_2_out),
    .sel(comparator_2_eq));
  assign bit_extender_2_out = {{31{comparator_2_eq}}, comparator_2_eq};  // Bit_Extender bit_extender_2
  Comparator #(.width(4)) comparator_3 (.a(multiplexer_2_out[7:4]), .b(4'b0000), .eq(comparator_3_eq));  // open: gt, lt
  assign and_2_out = bit_extender_2_out & 32'h8;  // AND_Gate and_2, 32 bits wide
  Multiplexer #(.width(4)) multiplexer_3 (
    .in0(multiplexer_2_out[7:4]), .in1(multiplexer_2_out[3:0]), .out(multiplexer_3_out), .sel(comparator_3_eq));
  assign bit_extender_3_out = {{31{comparator_3_eq}}, comparator_3_eq};  // Bit_Extender bit_extender_3
  Adder #(.width(32)) adder_1 (.a(and_2_out), .b(and_1_out), .out(adder_1_out));  // open: cin, cout
  Comparator #(.width(2)) comparator_4 (.a(multiplexer_3_out[3:2]), .b(2'b00), .eq(comparator_4_eq));  // open: gt, lt
  assign and_3_out = bit_extender_3_out & 32'h4;  // AND_Gate and_3, 32 bits wide
  Multiplexer #(.width(2)) multiplexer_4 (
    .in0(multiplexer_3_out[3:2]), .in1(multiplexer_3_out[1:0]), .out(multiplexer_4_out), .sel(comparator_4_eq));
  assign bit_extender_4_out = {{31{comparator_4_eq}}, comparator_4_eq};  // Bit_Extender bit_extender_4
  not not_1 (not_1_out, multiplexer_4_out[0]);
  not not_2 (not_2_out[0], multiplexer_4_out[1]);
  assign and_4_out = bit_extender_4_out & 32'h2;  // AND_Gate and_4, 32 bits wide
  Adder #(.width(32)) adder_2 (.a(and_3_out), .b(adder_1_out), .out(adder_2_out));  // open: cin, cout
  Adder #(.width(32)) adder_3 (.a(and_4_out), .b(adder_2_out), .out(adder_3_out));  // open: cin, cout
  and and_5 (and_5_out, not_1_out, not_2_out[0]);
  Adder #(.width(32)) adder_4 (
    .a({{31{1'b0}}, not_2_out[0]}), .b(adder_3_out), .out(res_low), .cin(and_5_out));  // open: cout

  assign res_high = {32{1'b0}};
endmodule

module Clo (
  input  [31:0] a,
  output [31:0] res_low,
  output [31:0] res_high
);

  wire [31:0] not_1_out;

  assign not_1_out = ~a;  // NOT_Gate not_1, 32 bits wide
  Clz clz_1 (.A(not_1_out), .res_low(res_low), .res_high(res_high));
endmodule

module RF (
  input  [4:0] Read0,
  input  [4:0] Read1,
  input  WriteReg,
  input  [4:0] Write,
  input  [31:0] Data,
  input  clk,
  input  rst,
  output [31:0] RegOut1,
  output [31:0] RegOut2,
  output [31:0] R0,
  output [31:0] R1,
  output [31:0] R2,
  output [31:0] R3,
  output [31:0] R4,
  output [31:0] R5,
  output [31:0] R6,
  output [31:0] R7,
  output [31:0] R8,
  output [31:0] R9,
  output [31:0] R10,
  output [31:0] R11,
  output [31:0] R12,
  output [31:0] R13,
  output [31:0] R14,
  output [31:0] R15,
  output [31:0] R16,
  output [31:0] R17,
  output [31:0] R18,
  output [31:0] R19,
  output [31:0] R20,
  output [31:0] R21,
  output [31:0] R22,
  output [31:0] R23,
  output [31:0] R24,
  output [31:0] R25,
  output [31:0] R26,
  output [31:0] R27,
  output [31:0] R28,
  output [31:0] R29,
  output [31:0] R30,
  output [31:0] R31
);

  wire decoder_1_out0, decoder_1_out1, decoder_1_out2, decoder_1_out3, decoder_1_out4, decoder_1_out5,
       decoder_1_out6, decoder_1_out7, decoder_1_out8, decoder_1_out9, decoder_1_out10, decoder_1_out11,
       decoder_1_out12, decoder_1_out13, decoder_1_out14, decoder_1_out15, decoder_1_out16, decoder_1_out17,
       decoder_1_out18, decoder_1_out19, decoder_1_out20, decoder_1_out21, decoder_1_out22, decoder_1_out23,
       decoder_1_out24, decoder_1_out25, decoder_1_out26, decoder_1_out27, decoder_1_out28, decoder_1_out29,
       decoder_1_out30, decoder_1_out31;

  Multiplexer #(.select(5), .width(32)) multiplexer_1 (
    .in0(R0), .in1(R1), .in2(R2), .in3(R3), .in4(R4), .in5(R5), .in6(R6), .in7(R7), .in8(R8), .in9(R9),
    .in10(R10), .in11(R11), .in12(R12), .in13(R13), .in14(R14), .in15(R15), .in16(R16), .in17(R17),
    .in18(R18), .in19(R19), .in20(R20), .in21(R21), .in22(R22), .in23(R23), .in24(R24), .in25(R25),
    .in26(R26), .in27(R27), .in28(R28), .in29(R29), .in30(R30), .in31(R31), .out(RegOut1), .sel(Read0));
  Decoder #(.select(5)) decoder_1 (
    .out0(decoder_1_out0), .out1(decoder_1_out1), .out2(decoder_1_out2), .out3(decoder_1_out3),
    .out4(decoder_1_out4), .out5(decoder_1_out5), .out6(decoder_1_out6), .out7(decoder_1_out7),
    .out8(decoder_1_out8), .out9(decoder_1_out9), .out10(decoder_1_out10), .out11(decoder_1_out11),
    .out12(decoder_1_out12), .out13(decoder_1_out13), .out14(decoder_1_out14), .out15(decoder_1_out15),
    .out16(decoder_1_out16), .out17(decoder_1_out17), .out18(decoder_1_out18), .out19(decoder_1_out19),
    .out20(decoder_1_out20), .out21(decoder_1_out21), .out22(decoder_1_out22), .out23(decoder_1_out23),
    .out24(decoder_1_out24), .out25(decoder_1_out25), .out26(decoder_1_out26), .out27(decoder_1_out27),
    .out28(decoder_1_out28), .out29(decoder_1_out29), .out30(decoder_1_out30), .out31(decoder_1_out31),
    .sel(Write), .en(WriteReg));
  Register #(.width(32)) Reg31 (.D(Data), .en(decoder_1_out31), .clk(clk), .Q(R31), .clr(rst));
  Register #(.width(32)) Reg30 (.D(Data), .en(decoder_1_out30), .clk(clk), .Q(R30), .clr(rst));
  Register #(.width(32)) register_1 (.D(Data), .en(decoder_1_out29), .clk(clk), .Q(R29), .clr(rst));
  Register #(.width(32)) register_2 (.D(Data), .en(decoder_1_out28), .clk(clk), .Q(R28), .clr(rst));
  Register #(.width(32)) register_3 (.D(Data), .en(decoder_1_out27), .clk(clk), .Q(R27), .clr(rst));
  Register #(.width(32)) register_4 (.D(Data), .en(decoder_1_out26), .clk(clk), .Q(R26), .clr(rst));
  Register #(.width(32)) register_5 (.D(Data), .en(decoder_1_out25), .clk(clk), .Q(R25), .clr(rst));
  Register #(.width(32)) register_6 (.D(Data), .en(decoder_1_out24), .clk(clk), .Q(R24), .clr(rst));
  Register #(.width(32)) register_7 (.D(Data), .en(decoder_1_out23), .clk(clk), .Q(R23), .clr(rst));
  Register #(.width(32)) register_8 (.D(Data), .en(decoder_1_out22), .clk(clk), .Q(R22), .clr(rst));
  Register #(.width(32)) register_9 (.D(Data), .en(decoder_1_out21), .clk(clk), .Q(R21), .clr(rst));
  Register #(.width(32)) register_10 (.D(Data), .en(decoder_1_out20), .clk(clk), .Q(R20), .clr(rst));
  Register #(.width(32)) register_11 (.D(Data), .en(decoder_1_out19), .clk(clk), .Q(R19), .clr(rst));
  Register #(.width(32)) register_12 (.D(Data), .en(decoder_1_out18), .clk(clk), .Q(R18), .clr(rst));
  Register #(.width(32)) register_13 (.D(Data), .en(decoder_1_out17), .clk(clk), .Q(R17), .clr(rst));
  Register #(.width(32)) register_14 (.D(Data), .en(decoder_1_out16), .clk(clk), .Q(R16), .clr(rst));
  Register #(.width(32)) register_15 (.D(Data), .en(decoder_1_out15), .clk(clk), .Q(R15), .clr(rst));
  Register #(.width(32)) register_16 (.D(Data), .en(decoder_1_out14), .clk(clk), .Q(R14), .clr(rst));
  Register #(.width(32)) register_17 (.D(Data), .en(decoder_1_out13), .clk(clk), .Q(R13), .clr(rst));
  Register #(.width(32)) register_18 (.D(Data), .en(decoder_1_out12), .clk(clk), .Q(R12), .clr(rst));
  Register #(.width(32)) register_19 (.D(Data), .en(decoder_1_out11), .clk(clk), .Q(R11), .clr(rst));
  Register #(.width(32)) register_20 (.D(Data), .en(decoder_1_out10), .clk(clk), .Q(R10), .clr(rst));
  Register #(.width(32)) register_21 (.D(Data), .en(decoder_1_out9), .clk(clk), .Q(R9), .clr(rst));
  Register #(.width(32)) register_22 (.D(Data), .en(decoder_1_out8), .clk(clk), .Q(R8), .clr(rst));
  Register #(.width(32)) register_23 (.D(Data), .en(decoder_1_out7), .clk(clk), .Q(R7), .clr(rst));
  Register #(.width(32)) register_24 (.D(Data), .en(decoder_1_out6), .clk(clk), .Q(R6), .clr(rst));
  Register #(.width(32)) register_25 (.D(Data), .en(decoder_1_out5), .clk(clk), .Q(R5), .clr(rst));
  Register #(.width(32)) register_26 (.D(Data), .en(decoder_1_out4), .clk(clk), .Q(R4), .clr(rst));
  Register #(.width(32)) register_27 (.D(Data), .en(decoder_1_out3), .clk(clk), .Q(R3), .clr(rst));
  Register #(.width(32)) register_28 (.D(Data), .en(decoder_1_out2), .clk(clk), .Q(R2), .clr(rst));
  Register #(.width(32)) Reg1 (.D(Data), .en(decoder_1_out1), .clk(clk), .Q(R1), .clr(rst));
  Register #(.width(32)) Reg0 (.D({32{1'b0}}), .clk(clk), .Q(R0), .clr(rst));  // open: en
  Multiplexer #(.select(5), .width(32)) multiplexer_2 (
    .in0(R0), .in1(R1), .in2(R2), .in3(R3), .in4(R4), .in5(R5), .in6(R6), .in7(R7), .in8(R8), .in9(R9),
    .in10(R10), .in11(R11), .in12(R12), .in13(R13), .in14(R14), .in15(R15), .in16(R16), .in17(R17),
    .in18(R18), .in19(R19), .in20(R20), .in21(R21), .in22(R22), .in23(R23), .in24(R24), .in25(R25),
    .in26(R26), .in27(R27), .in28(R28), .in29(R29), .in30(R30), .in31(R31), .out(RegOut2), .sel(Read1));
endmodule

module MEM (
  input  Wen,
  input  Jen,
  input  clk,
  input  [8:0] Addr,
  input  [31:0] Din,
  input  [31:0] Jin,
  output [31:0] Dout,
  output [31:0] Jout
);

  wire decoder_1_out0, decoder_1_out1, decoder_1_out2, decoder_1_out3, decoder_1_out4, decoder_1_out5,
       decoder_1_out6, decoder_1_out7;
  wire [31:0] mem256_1_dout, mem256_1_jout, mem256_2_dout, mem256_2_jout, mem256_3_dout, mem256_3_jout,
       mem256_4_dout, mem256_4_jout, mem256_5_dout, mem256_5_jout, mem256_6_dout, mem256_6_jout,
       mem256_7_dout, mem256_7_jout, mem256_8_dout;

  Decoder #(.select(3)) decoder_1 (
    .out0(decoder_1_out0), .out1(decoder_1_out1), .out2(decoder_1_out2), .out3(decoder_1_out3),
    .out4(decoder_1_out4), .out5(decoder_1_out5), .out6(decoder_1_out6), .out7(decoder_1_out7),
    .sel(Addr[8:6]), .en(Wen));
  Mem256 mem256_1 (
    .Wen(decoder_1_out0), .Jen(Jen), .clk(clk), .Addr(Addr[5:0]), .Din(Din), .Jin(Jin), .Dout(mem256_1_dout),
    .Jout(mem256_1_jout));
  Mem256 mem256_2 (
    .Wen(decoder_1_out1), .Jen(Jen), .clk(clk), .Addr(Addr[5:0]), .Din(Din), .Jin(mem256_1_jout),
    .Dout(mem256_2_dout), .Jout(mem256_2_jout));
  Mem256 mem256_3 (
    .Wen(decoder_1_out2), .Jen(Jen), .clk(clk), .Addr(Addr[5:0]), .Din(Din), .Jin(mem256_2_jout),
    .Dout(mem256_3_dout), .Jout(mem256_3_jout));
  Mem256 mem256_4 (
    .Wen(decoder_1_out3), .Jen(Jen), .clk(clk), .Addr(Addr[5:0]), .Din(Din), .Jin(mem256_3_jout),
    .Dout(mem256_4_dout), .Jout(mem256_4_jout));
  Mem256 mem256_5 (
    .Wen(decoder_1_out4), .Jen(Jen), .clk(clk), .Addr(Addr[5:0]), .Din(Din), .Jin(mem256_4_jout),
    .Dout(mem256_5_dout), .Jout(mem256_5_jout));
  Mem256 mem256_6 (
    .Wen(decoder_1_out5), .Jen(Jen), .clk(clk), .Addr(Addr[5:0]), .Din(Din), .Jin(mem256_5_jout),
    .Dout(mem256_6_dout), .Jout(mem256_6_jout));
  Mem256 mem256_7 (
    .Wen(decoder_1_out6), .Jen(Jen), .clk(clk), .Addr(Addr[5:0]), .Din(Din), .Jin(mem256_6_jout),
    .Dout(mem256_7_dout), .Jout(mem256_7_jout));
  Mem256 mem256_8 (
    .Wen(decoder_1_out7), .Jen(Jen), .clk(clk), .Addr(Addr[5:0]), .Din(Din), .Jin(mem256_7_jout),
    .Dout(mem256_8_dout), .Jout(Jout));
  Multiplexer #(.select(3), .width(32)) multiplexer_1 (
    .in0(mem256_1_dout), .in1(mem256_2_dout), .in2(mem256_3_dout), .in3(mem256_4_dout), .in4(mem256_5_dout),
    .in5(mem256_6_dout), .in6(mem256_7_dout), .in7(mem256_8_dout), .out(Dout), .sel(Addr[8:6]));

  // Other names for the same wires on the sheet: Addr_low[5:0] = Addr[5:0]; Addr_high[2:0] = Addr[8:6]
endmodule

module Mem256 (
  input  Wen,
  input  Jen,
  input  clk,
  input  [5:0] Addr,
  input  [31:0] Din,
  input  [31:0] Jin,
  output [31:0] Dout,
  output [31:0] Jout
);

  wire decoder_1_out0, decoder_1_out1, decoder_1_out2, decoder_1_out3, decoder_1_out4, decoder_1_out5,
       decoder_1_out6, decoder_1_out7;
  wire [31:0] mem32_1_dout, mem32_1_jout, mem32_2_dout, mem32_2_jout, mem32_3_dout, mem32_3_jout,
       mem32_4_dout, mem32_4_jout, mem32_5_dout, mem32_5_jout, mem32_6_dout, mem32_6_jout, mem32_7_dout,
       mem32_7_jout, mem32_8_dout;

  Decoder #(.select(3)) decoder_1 (
    .out0(decoder_1_out0), .out1(decoder_1_out1), .out2(decoder_1_out2), .out3(decoder_1_out3),
    .out4(decoder_1_out4), .out5(decoder_1_out5), .out6(decoder_1_out6), .out7(decoder_1_out7),
    .sel(Addr[5:3]), .en(Wen));
  Mem32 mem32_1 (
    .Wen(decoder_1_out0), .Jen(Jen), .clk(clk), .Addr(Addr[2:0]), .Din(Din), .Jin(Jin), .Dout(mem32_1_dout),
    .Jout(mem32_1_jout));
  Mem32 mem32_2 (
    .Wen(decoder_1_out1), .Jen(Jen), .clk(clk), .Addr(Addr[2:0]), .Din(Din), .Jin(mem32_1_jout),
    .Dout(mem32_2_dout), .Jout(mem32_2_jout));
  Mem32 mem32_3 (
    .Wen(decoder_1_out2), .Jen(Jen), .clk(clk), .Addr(Addr[2:0]), .Din(Din), .Jin(mem32_2_jout),
    .Dout(mem32_3_dout), .Jout(mem32_3_jout));
  Mem32 mem32_4 (
    .Wen(decoder_1_out3), .Jen(Jen), .clk(clk), .Addr(Addr[2:0]), .Din(Din), .Jin(mem32_3_jout),
    .Dout(mem32_4_dout), .Jout(mem32_4_jout));
  Mem32 mem32_5 (
    .Wen(decoder_1_out4), .Jen(Jen), .clk(clk), .Addr(Addr[2:0]), .Din(Din), .Jin(mem32_4_jout),
    .Dout(mem32_5_dout), .Jout(mem32_5_jout));
  Mem32 mem32_6 (
    .Wen(decoder_1_out5), .Jen(Jen), .clk(clk), .Addr(Addr[2:0]), .Din(Din), .Jin(mem32_5_jout),
    .Dout(mem32_6_dout), .Jout(mem32_6_jout));
  Mem32 mem32_7 (
    .Wen(decoder_1_out6), .Jen(Jen), .clk(clk), .Addr(Addr[2:0]), .Din(Din), .Jin(mem32_6_jout),
    .Dout(mem32_7_dout), .Jout(mem32_7_jout));
  Mem32 mem32_8 (
    .Wen(decoder_1_out7), .Jen(Jen), .clk(clk), .Addr(Addr[2:0]), .Din(Din), .Jin(mem32_7_jout),
    .Dout(mem32_8_dout), .Jout(Jout));
  Multiplexer #(.select(3), .width(32)) multiplexer_1 (
    .in0(mem32_1_dout), .in1(mem32_2_dout), .in2(mem32_3_dout), .in3(mem32_4_dout), .in4(mem32_5_dout),
    .in5(mem32_6_dout), .in6(mem32_7_dout), .in7(mem32_8_dout), .out(Dout), .sel(Addr[5:3]));

  // Other names for the same wires on the sheet: Addr_low[2:0] = Addr[2:0]; Addr_high[2:0] = Addr[5:3]
endmodule

module Mem32 (
  input  Wen,
  input  Jen,
  input  clk,
  input  [2:0] Addr,
  input  [31:0] Din,
  input  [31:0] Jin,
  output [31:0] Dout,
  output [31:0] Jout
);

  wire decoder_1_out0, decoder_1_out1, decoder_1_out2, decoder_1_out3, decoder_1_out4, decoder_1_out5,
       decoder_1_out6, decoder_1_out7, or_1_out, or_2_out, or_3_out, or_4_out, or_5_out, or_6_out, or_7_out,
       or_8_out;
  wire [31:0] multiplexer_1_out, multiplexer_2_out, multiplexer_3_out, multiplexer_4_out, multiplexer_5_out,
       multiplexer_6_out, multiplexer_7_out, multiplexer_8_out, register_1_q, register_2_q, register_3_q,
       register_4_q, register_5_q, register_6_q, register_7_q;

  Decoder #(.select(3)) decoder_1 (
    .out0(decoder_1_out0), .out1(decoder_1_out1), .out2(decoder_1_out2), .out3(decoder_1_out3),
    .out4(decoder_1_out4), .out5(decoder_1_out5), .out6(decoder_1_out6), .out7(decoder_1_out7), .sel(Addr),
    .en(Wen));
  Multiplexer #(.width(32)) multiplexer_1 (.in0(Din), .in1(Jin), .out(multiplexer_1_out), .sel(Jen));
  Multiplexer #(.width(32)) multiplexer_2 (.in0(Din), .in1(register_1_q), .out(multiplexer_2_out), .sel(Jen));
  Multiplexer #(.width(32)) multiplexer_3 (.in0(Din), .in1(register_2_q), .out(multiplexer_3_out), .sel(Jen));
  Multiplexer #(.width(32)) multiplexer_4 (.in0(Din), .in1(register_3_q), .out(multiplexer_4_out), .sel(Jen));
  Multiplexer #(.width(32)) multiplexer_5 (.in0(Din), .in1(register_4_q), .out(multiplexer_5_out), .sel(Jen));
  Multiplexer #(.width(32)) multiplexer_6 (.in0(Din), .in1(register_5_q), .out(multiplexer_6_out), .sel(Jen));
  Multiplexer #(.width(32)) multiplexer_7 (.in0(Din), .in1(register_6_q), .out(multiplexer_7_out), .sel(Jen));
  Multiplexer #(.width(32)) multiplexer_8 (.in0(Din), .in1(register_7_q), .out(multiplexer_8_out), .sel(Jen));
  or or_1 (or_1_out, Jen, decoder_1_out0);
  or or_2 (or_2_out, Jen, decoder_1_out1);
  or or_3 (or_3_out, Jen, decoder_1_out2);
  or or_4 (or_4_out, Jen, decoder_1_out3);
  or or_5 (or_5_out, Jen, decoder_1_out4);
  or or_6 (or_6_out, Jen, decoder_1_out5);
  or or_7 (or_7_out, Jen, decoder_1_out6);
  or or_8 (or_8_out, Jen, decoder_1_out7);
  Register #(.width(32)) register_1 (.D(multiplexer_1_out), .en(or_1_out), .clk(clk), .Q(register_1_q));  // open: clr
  Register #(.width(32)) register_2 (.D(multiplexer_2_out), .en(or_2_out), .clk(clk), .Q(register_2_q));  // open: clr
  Register #(.width(32)) register_3 (.D(multiplexer_3_out), .en(or_3_out), .clk(clk), .Q(register_3_q));  // open: clr
  Register #(.width(32)) register_4 (.D(multiplexer_4_out), .en(or_4_out), .clk(clk), .Q(register_4_q));  // open: clr
  Register #(.width(32)) register_5 (.D(multiplexer_5_out), .en(or_5_out), .clk(clk), .Q(register_5_q));  // open: clr
  Register #(.width(32)) register_6 (.D(multiplexer_6_out), .en(or_6_out), .clk(clk), .Q(register_6_q));  // open: clr
  Register #(.width(32)) register_7 (.D(multiplexer_7_out), .en(or_7_out), .clk(clk), .Q(register_7_q));  // open: clr
  Register #(.width(32)) register_8 (.D(multiplexer_8_out), .en(or_8_out), .clk(clk), .Q(Jout));  // open: clr
  Multiplexer #(.select(3), .width(32)) multiplexer_9 (
    .in0(register_1_q), .in1(register_2_q), .in2(register_3_q), .in3(register_4_q), .in4(register_5_q),
    .in5(register_6_q), .in6(register_7_q), .in7(Jout), .out(Dout), .sel(Addr));
endmodule

module Control (
  input  [5:0] opcode,
  input  [5:0] funct,
  output Branch,
  output [1:0] Jump,
  output [1:0] RegDst,
  output RegWrite,
  output [1:0] ALUOp,
  output ALUSrc,
  output MemWrite,
  output [2:0] MemtoReg
);

  wire addi, and_4_out, comparator_9_eq, comparator_10_eq, comparator_11_eq, j, lw, mfhi, not_1_out, Rtype,
       slti;

  Comparator #(.width(6)) comparator_1 (.a(opcode), .b({6{1'b0}}), .eq(Rtype));  // open: gt, lt
  Comparator #(.width(6)) comparator_2 (.a(opcode), .b(6'b001000), .eq(addi));  // open: gt, lt
  Comparator #(.width(6)) comparator_3 (.a(opcode), .b(6'b100011), .eq(lw));  // open: gt, lt
  Comparator #(.width(6)) comparator_4 (.a(opcode), .b(6'b101011), .eq(MemWrite));  // open: gt, lt
  Comparator #(.width(6)) comparator_5 (.a(opcode), .b(6'b000010), .eq(j));  // open: gt, lt
  Comparator #(.width(6)) comparator_6 (.a(opcode), .b(6'b000011), .eq(RegDst[1]));  // open: gt, lt
  Comparator #(.width(6)) comparator_7 (.a(opcode), .b(6'b001010), .eq(slti));  // open: gt, lt
  Comparator #(.width(6)) comparator_8 (.a(opcode), .b(6'b000101), .eq(Branch));  // open: gt, lt
  Comparator #(.width(6)) comparator_9 (.a(funct), .b(6'b001000), .eq(comparator_9_eq));  // open: gt, lt
  Comparator #(.width(6)) comparator_10 (.a(funct), .b(6'b010000), .eq(comparator_10_eq));  // open: gt, lt
  Comparator #(.width(6)) comparator_11 (.a(funct), .b(6'b010010), .eq(comparator_11_eq));  // open: gt, lt
  and and_1 (Jump[1], Rtype, comparator_9_eq);
  and and_2 (mfhi, Rtype, comparator_10_eq);
  and and_3 (MemtoReg[2], Rtype, comparator_11_eq);
  not not_1 (not_1_out, Jump[1]);
  or or_1 (Jump[0], j, RegDst[1]);
  and and_4 (and_4_out, Rtype, not_1_out);
  or or_2 (RegDst[0], addi, lw, slti);
  or or_3 (ALUOp[1], slti, Rtype);
  or or_4 (MemtoReg[0], lw, mfhi);
  or or_5 (MemtoReg[1], RegDst[1], mfhi);
  or or_6 (ALUOp[0], slti, Branch);
  or or_7 (ALUSrc, Rtype, Branch);
  or or_8 (RegWrite, and_4_out, addi, lw, RegDst[1], slti);

  // Other names for the same wires on the sheet: bne = Branch; jr = Jump[1]; mflo = MemtoReg[2]; jal = RegDst[1];
  //   sw = MemWrite
endmodule

module ALUControl (
  input  [5:0] funct,
  input  [1:0] ALUOp,
  output [3:0] operation,
  output HIWrite,
  output LOWrite
);

  wire comparator_1_eq, comparator_2_eq, comparator_3_eq, comparator_4_eq, comparator_5_eq, comparator_6_eq,
       comparator_7_eq;
  wire [3:0] multiplexer_1_out, multiplexer_2_out, multiplexer_3_out, multiplexer_4_out, multiplexer_5_out,
       multiplexer_6_out;

  Comparator #(.width(6)) comparator_1 (.a(funct), .b(6'b100010), .eq(comparator_1_eq));  // open: gt, lt
  Comparator #(.width(6)) comparator_2 (.a(funct), .b(6'b100100), .eq(comparator_2_eq));  // open: gt, lt
  Comparator #(.width(6)) comparator_3 (.a(funct), .b(6'b100101), .eq(comparator_3_eq));  // open: gt, lt
  Comparator #(.width(6)) comparator_4 (.a(funct), .b(6'b100110), .eq(comparator_4_eq));  // open: gt, lt
  Comparator #(.width(6)) comparator_5 (.a(funct), .b(6'b011010), .eq(comparator_5_eq));  // open: gt, lt
  Comparator #(.width(6)) comparator_6 (.a(funct), .b({6{1'b0}}), .eq(comparator_6_eq));  // open: gt, lt
  Comparator #(.width(2)) comparator_7 (.a(ALUOp), .b(2'b10), .eq(comparator_7_eq));  // open: gt, lt
  Multiplexer #(.width(4)) multiplexer_1 (.in0(4'b0000), .in1(4'b0001), .out(multiplexer_1_out), .sel(comparator_1_eq));
  Multiplexer #(.width(4)) multiplexer_2 (
    .in0(multiplexer_1_out), .in1(4'b0100), .out(multiplexer_2_out), .sel(comparator_2_eq));
  Multiplexer #(.width(4)) multiplexer_3 (
    .in0(multiplexer_2_out), .in1(4'b0101), .out(multiplexer_3_out), .sel(comparator_3_eq));
  and and_1 (HIWrite, comparator_5_eq, comparator_7_eq);
  Multiplexer #(.width(4)) multiplexer_4 (
    .in0(multiplexer_3_out), .in1(4'b0110), .out(multiplexer_4_out), .sel(comparator_4_eq));
  Multiplexer #(.width(4)) multiplexer_5 (
    .in0(multiplexer_4_out), .in1(4'b0011), .out(multiplexer_5_out), .sel(comparator_5_eq));
  Multiplexer #(.width(4)) multiplexer_6 (
    .in0(multiplexer_5_out), .in1(4'b1110), .out(multiplexer_6_out), .sel(comparator_6_eq));
  Multiplexer #(.select(2), .width(4)) multiplexer_7 (
    .in0(4'b0000), .in1(4'b0001), .in2(multiplexer_6_out), .in3(4'b1101), .out(operation), .sel(ALUOp));

  assign LOWrite = HIWrite;
endmodule

module IFID (
  input  WriteEnable,
  input  [8:0] PC_in,
  input  [31:0] Instruction_in,
  input  clk,
  input  reset,
  output [8:0] PC,
  output [31:0] Instruction
);

  Register #(.width(9)) PCReg (.D(PC_in), .en(WriteEnable), .clk(clk), .Q(PC), .clr(reset));
  Register #(.width(32)) IR (.D(Instruction_in), .en(WriteEnable), .clk(clk), .Q(Instruction), .clr(reset));
endmodule

module IDEX (
  input  WriteEnable,
  input  [1:0] RegDst_in,
  input  RegWrite_in,
  input  [1:0] ALUOp_in,
  input  ALUSrc_in,
  input  MemWrite_in,
  input  [2:0] MemtoReg_in,
  input  [8:0] PC_in,
  input  [5:0] funct_in,
  input  [4:0] shamt_in,
  input  [31:0] imm_in,
  input  [31:0] ReadData1_in,
  input  [31:0] ReadData2_in,
  input  [4:0] rt_in,
  input  [4:0] rd_in,
  input  clk,
  input  reset,
  output [1:0] RegDst,
  output RegWrite,
  output [1:0] ALUOp,
  output ALUSrc,
  output MemWrite,
  output [2:0] MemtoReg,
  output [8:0] PC,
  output [5:0] funct,
  output [4:0] shamt,
  output [31:0] imm,
  output [31:0] ReadData1,
  output [31:0] ReadData2,
  output [4:0] rt,
  output [4:0] rd
);

  Register #(.width(2)) register_1 (.D(RegDst_in), .en(WriteEnable), .clk(clk), .Q(RegDst), .clr(reset));
  Register #(.width(1)) register_2 (.D(RegWrite_in), .en(WriteEnable), .clk(clk), .Q(RegWrite), .clr(reset));
  Register #(.width(2)) register_3 (.D(ALUOp_in), .en(WriteEnable), .clk(clk), .Q(ALUOp), .clr(reset));
  Register #(.width(1)) register_4 (.D(ALUSrc_in), .en(WriteEnable), .clk(clk), .Q(ALUSrc), .clr(reset));
  Register #(.width(1)) register_5 (.D(MemWrite_in), .en(WriteEnable), .clk(clk), .Q(MemWrite), .clr(reset));
  Register #(.width(3)) register_6 (.D(MemtoReg_in), .en(WriteEnable), .clk(clk), .Q(MemtoReg), .clr(reset));
  Register #(.width(9)) register_7 (.D(PC_in), .en(WriteEnable), .clk(clk), .Q(PC), .clr(reset));
  Register #(.width(6)) register_8 (.D(funct_in), .en(WriteEnable), .clk(clk), .Q(funct), .clr(reset));
  Register #(.width(5)) register_9 (.D(shamt_in), .en(WriteEnable), .clk(clk), .Q(shamt), .clr(reset));
  Register #(.width(32)) register_10 (.D(imm_in), .en(WriteEnable), .clk(clk), .Q(imm), .clr(reset));
  Register #(.width(32)) register_11 (.D(ReadData1_in), .en(WriteEnable), .clk(clk), .Q(ReadData1), .clr(reset));
  Register #(.width(32)) register_12 (.D(ReadData2_in), .en(WriteEnable), .clk(clk), .Q(ReadData2), .clr(reset));
  Register #(.width(5)) register_13 (.D(rt_in), .en(WriteEnable), .clk(clk), .Q(rt), .clr(reset));
  Register #(.width(5)) register_14 (.D(rd_in), .en(WriteEnable), .clk(clk), .Q(rd), .clr(reset));
endmodule

module EXMEM (
  input  WriteEnable,
  input  [1:0] RegDst_in,
  input  RegWrite_in,
  input  MemWrite_in,
  input  [2:0] MemtoReg_in,
  input  [8:0] PC_in,
  input  [31:0] ALUResult_in,
  input  [31:0] HI_in,
  input  [31:0] LO_in,
  input  [31:0] ReadData2_in,
  input  [4:0] rt_in,
  input  [4:0] rd_in,
  input  InstDone_in,
  input  clk,
  input  reset,
  output [1:0] RegDst,
  output RegWrite,
  output MemWrite,
  output [2:0] MemtoReg,
  output [8:0] PC,
  output [31:0] ALUResult,
  output [31:0] HI,
  output [31:0] LO,
  output [31:0] ReadData2,
  output [4:0] rt,
  output [4:0] rd,
  output InstDone
);

  Register #(.width(2)) register_1 (.D(RegDst_in), .en(WriteEnable), .clk(clk), .Q(RegDst), .clr(reset));
  Register #(.width(1)) register_2 (.D(RegWrite_in), .en(WriteEnable), .clk(clk), .Q(RegWrite), .clr(reset));
  Register #(.width(1)) register_3 (.D(MemWrite_in), .en(WriteEnable), .clk(clk), .Q(MemWrite), .clr(reset));
  Register #(.width(3)) register_4 (.D(MemtoReg_in), .en(WriteEnable), .clk(clk), .Q(MemtoReg), .clr(reset));
  Register #(.width(9)) register_5 (.D(PC_in), .en(WriteEnable), .clk(clk), .Q(PC), .clr(reset));
  Register #(.width(32)) register_6 (.D(ALUResult_in), .en(WriteEnable), .clk(clk), .Q(ALUResult), .clr(reset));
  Register #(.width(32)) register_7 (.D(HI_in), .en(WriteEnable), .clk(clk), .Q(HI), .clr(reset));
  Register #(.width(32)) register_8 (.D(LO_in), .en(WriteEnable), .clk(clk), .Q(LO), .clr(reset));
  Register #(.width(32)) register_9 (.D(ReadData2_in), .en(WriteEnable), .clk(clk), .Q(ReadData2), .clr(reset));
  Register #(.width(5)) register_10 (.D(rt_in), .en(WriteEnable), .clk(clk), .Q(rt), .clr(reset));
  Register #(.width(5)) register_11 (.D(rd_in), .en(WriteEnable), .clk(clk), .Q(rd), .clr(reset));
  Register #(.width(1)) register_12 (.D(InstDone_in), .en(WriteEnable), .clk(clk), .Q(InstDone), .clr(reset));
endmodule

module MEMWB (
  input  WriteEnable,
  input  [1:0] RegDst_in,
  input  RegWrite_in,
  input  [2:0] MemtoReg_in,
  input  [8:0] PC_in,
  input  [31:0] HI_in,
  input  [31:0] LO_in,
  input  [31:0] MemRead_in,
  input  [31:0] ALUResult_in,
  input  [4:0] rt_in,
  input  [4:0] rd_in,
  input  InstDone_in,
  input  clk,
  input  reset,
  output [1:0] RegDst,
  output RegWrite,
  output [2:0] MemtoReg,
  output [8:0] PC,
  output [31:0] HI,
  output [31:0] LO,
  output [31:0] MemRead,
  output [31:0] ALUResult,
  output [4:0] rt,
  output [4:0] rd,
  output InstDone
);

  Register #(.width(2)) register_1 (.D(RegDst_in), .en(WriteEnable), .clk(clk), .Q(RegDst), .clr(reset));
  Register #(.width(1)) register_2 (.D(RegWrite_in), .en(WriteEnable), .clk(clk), .Q(RegWrite), .clr(reset));
  Register #(.width(3)) register_3 (.D(MemtoReg_in), .en(WriteEnable), .clk(clk), .Q(MemtoReg), .clr(reset));
  Register #(.width(9)) register_4 (.D(PC_in), .en(WriteEnable), .clk(clk), .Q(PC), .clr(reset));
  Register #(.width(32)) register_5 (.D(HI_in), .en(WriteEnable), .clk(clk), .Q(HI), .clr(reset));
  Register #(.width(32)) register_6 (.D(LO_in), .en(WriteEnable), .clk(clk), .Q(LO), .clr(reset));
  Register #(.width(32)) register_7 (.D(MemRead_in), .en(WriteEnable), .clk(clk), .Q(MemRead), .clr(reset));
  Register #(.width(32)) register_8 (.D(ALUResult_in), .en(WriteEnable), .clk(clk), .Q(ALUResult), .clr(reset));
  Register #(.width(5)) register_9 (.D(rt_in), .en(WriteEnable), .clk(clk), .Q(rt), .clr(reset));
  Register #(.width(5)) register_10 (.D(rd_in), .en(WriteEnable), .clk(clk), .Q(rd), .clr(reset));
  Register #(.width(1)) register_11 (.D(InstDone_in), .en(WriteEnable), .clk(clk), .Q(InstDone), .clr(reset));
endmodule
